# Fritzing sketch Fritzing_file (saved by Fritzing 1.0.4)
breadboards: 1

parts:
  Load_Cell1 = Load Cell - Red/white/black/green
  Module1 = Relay
  Module2 = Relay
  e-radionica_com1 = LM393 LDR breakout [part_number=100027]
  Part1 = Soil Moisture Sensor
  J1 = DHT11 basic temperature-humidity sensor [form="♂ (male)" package=THT]
  module1 = MQ-2 Gas Sensor
  ds18b20_probe1 = ds18b20 probe
  esp1 = ESP32 DevKitc V4

nets:
  N1: Load_Cell1.wire1, esp1.IO19
  VCC: Load_Cell1.wire2, Module1.power, Module2.power, e-radionica_com1.VCC, Part1.VCC, J1.VCC, module1.VCC, ds18b20_probe1.pin1, esp1.5V
  GND: Load_Cell1.wire3, Module1.ground, Module2.ground, e-radionica_com1.GND, Part1.GND, J1.GND, module1.GND, ds18b20_probe1.pin3, esp1.GND
  N2: Load_Cell1.wire4, esp1.IO18
  N3: Module1.signal, esp1.IO27
  N4: Module2.signal, esp1.IO26
  N5: e-radionica_com1.AO, esp1.IO32
  N6: Part1.SIG, esp1.IO35
  N7: J1.OUT, esp1.IO15
  N8: module1.AO, esp1.IO34
  N9: ds18b20_probe1.pin2, esp1.IO4

custom parts:
  Load Cell - Red/white/black/green: A rectangle load cell/weighting pressure Sensor with four wires - Red, white, black, green. Normally corresponding with E+, E-, A+, A- respectively.
  DHT11 basic temperature-humidity sensor: The DHT11 is a basic, ultra low-cost digital temperature and humidity sensor. It uses a capacitive humidity sensor and a thermistor to measure the surrounding air, and spits out a digital signal on the data pin (no analog input pins needed). Its fairly simple to use, but requires careful timing to grab data. The only real downside of this sensor is you can only get new data from it once every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
  MQ-2 Gas Sensor: MQ-2 Gas Sensor module of SunFounder Sensor Kit
  ESP32 DevKitc V4: ESP32-DevKitC board with ESP32-WROOM-32 module. ESP32-DevKitC V4 is a small-sized ESP32-based development board produced by Espressif. Most of the pins on the ESP module are broken out to the pin headers on the board. The pins D0, D1, D2, D3, CMD and CLK are used internally for communication between ESP32 and SPI flash memory. They are grouped on both sides near the USB connector. Avoid using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
